# Fritzing sketch CAN Bus Shield (saved by Fritzing 0.9.1b)
perfboards: 1

parts:
  IC1 = IC, DIP package, 18 pins [chip_label=MCP2515]
  IC2 = IC, DIP package, 8 pins [chip_label=2551]
  XTAL1 = Crystal [frequency="16 Mhz" package=THT]
  C1 = Ceramic Capacitor [capacitance=10pF part_number=22pF package="100 mil [THT, multilayer]"]
  C2 = Ceramic Capacitor [capacitance=10pF part_number=22pF package="100 mil [THT, multilayer]"]
  J1 = MAGJACK-2 [package=magjack-19938]  # not connected

nets:
  N1: IC1.pin1, IC2.pin1
  N2: IC1.pin2, IC2.pin4
  N3: IC1.pin7, C1.1
  N4: IC1.pin8, XTAL1.pin_1, C2.0
  N5: IC1.pin9, C1.0, C2.1
